# Fritzing sketch digitalInEvery (saved by Fritzing 0.9.4)
breadboards: 1

parts:
  Part1 = Arduino Nano Every
  LED1 = LED - 5mm [color="Red (633nm)" package="5 mm [THT]"]
  S2 = Pushbutton [package="[THT]"]
  R2 = Resistor [tolerance=±5% resistance=10k package=THT]

nets:
  N1: Part1.RESET, Part1.A7
  N2: Part1.GND, Part1.D2, Part1.D13~, LED1.cathode, LED1.anode, S2.Pin_1, S2.Pin_2, R2.Pin_0, R2.Pin_1
  N3: Part1.D11/MOSI, Part1.+5V, S2.Pin_3, S2.Pin_4

custom parts:
  Arduino Nano Every: The Nano Every is Arduino’s 5V compatible board in the smallest available form factor: 45x18mm! The Arduino Nano is the preferred board for many projects requiring a small and easy to use microcontroller board. The small footprint and low price, make the Nano Every particularly suited for wearable inventions, low cost robotics, electronic musical instruments, and general use to control smaller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
